# Fritzing sketch yun-lpd8806-5v-external (saved by Fritzing 0.9.0b)
breadboards: 1

parts:
  Part1 = Arduino Yun
  LPD8806_RGB_LED_Strip1 = LPD8806 RGB LED Strip
  JACK1 = 2.1mm Barrel Jack with Terminal Block
  C1 = Electrolytic Capacitor [capacitance=1000µF package="300 mil [THT, electrolytic]"]

nets:
  N1: Part1.D13/SCK, LPD8806_RGB_LED_Strip1.CI
  N2: Part1.D3_PWM, LPD8806_RGB_LED_Strip1.DI
  GND: Part1.GND, LPD8806_RGB_LED_Strip1.GND, JACK1.NEG, C1.-
  VIN: Part1.VIN, LPD8806_RGB_LED_Strip1.+5V, JACK1.POS, C1.+

custom parts:
  LPD8806 RGB LED Strip: Digitally addressable RGB LED strip
