# Fritzing sketch yun-neopixel-5v-external (saved by Fritzing 0.9.0b)
breadboards: 1

parts:
  NEOPIXEL1 = Neopixel Strip -- White (60/m)
  JACK1 = 2.1mm Barrel Jack with Terminal Block
  C1 = Electrolytic Capacitor [capacitance=1000μF package="1010 [SMD, electrolytic]"]
  R1 = Resistor [tolerance=±5% resistance=220 package=THT]
  Part2 = Arduino Yun

nets:
  N1: NEOPIXEL1.+5V, R1.Pin_0
  N2: NEOPIXEL1.DI, JACK1.POS, C1.+, Part2.VIN
  GND: NEOPIXEL1.GND, JACK1.NEG, C1.-, Part2.GND
  N3: R1.Pin_1, Part2.D3_PWM

notes:
  Capacitor should be at least 1000 µF, 6.3V
  Resistor should be between 300 and 500 ohm

custom parts:
  Neopixel Strip -- White (60/m): Neopixel Strip, White, 60 pixels per meter.
